// Logisim project Boolean_Equation.circ as structural Verilog: 2 circuits, main circuit main
module main (
  input  in_1,
  input  in_2,
  input  in_3,
  input  in_4,
  output out_5
);

  eqn_1 eqn_1_1 (.A(in_1), .B(in_2), .C(in_3), .D(in_4), .F(out_5));
endmodule

module eqn_1 (
  input  A,
  input  B,
  input  C,
  input  D,
  output F
);

  wire G1_out, G2_out, G3_out, G4_out;

  and G1 (G1_out, ~A, ~B, C, ~D);  // AND_Gate
  and G2 (G2_out, ~A, B, C, D);  // AND_Gate
  and G3 (G3_out, A, ~B, C, ~D);  // AND_Gate
  and G4 (G4_out, A, B, C, ~D);  // AND_Gate
  or G5 (F, G1_out, G2_out, G3_out, G4_out);

  // Notes on the sheet:
  //   (A'B'CD') + (A'BCD) + (AB'CD')+(ABCD')
endmodule
