// Logisim project Counter_lab.circ as structural Verilog: 4 circuits, main circuit main
module main (
  input  in_1
);

  wire clock_1_out, j_k_ff_1_q, j_k_ff_1_qn, j_k_ff_2_q, j_k_ff_2_qn, j_k_ff_3_q, j_k_ff_3_qn, j_k_ff_4_q,
       j_k_ff_4_qn;

  Clock clock_1 (.out(clock_1_out));
  J_K_Flip_Flop j_k_ff_1 (
    .J(in_1), .K(in_1), .clk(clock_1_out), .Q(j_k_ff_1_q), .Qn(j_k_ff_1_qn));  // open: preset, reset
  // NoConnect on j_k_ff_1_qn
  LED A (.in(j_k_ff_4_q));
  J_K_Flip_Flop j_k_ff_2 (
    .J(in_1), .K(in_1), .clk(j_k_ff_1_q), .Q(j_k_ff_2_q), .Qn(j_k_ff_2_qn));  // open: preset, reset
  LED B (.in(j_k_ff_3_q));
  LED C (.in(j_k_ff_2_q));
  // NoConnect on j_k_ff_2_qn
  LED D (.in(j_k_ff_1_q));
  J_K_Flip_Flop j_k_ff_3 (
    .J(in_1), .K(in_1), .clk(j_k_ff_2_q), .Q(j_k_ff_3_q), .Qn(j_k_ff_3_qn));  // open: preset, reset
  // NoConnect on j_k_ff_3_qn
  J_K_Flip_Flop j_k_ff_4 (
    .J(in_1), .K(in_1), .clk(j_k_ff_3_q), .Q(j_k_ff_4_q), .Qn(j_k_ff_4_qn));  // open: preset, reset
  // NoConnect on j_k_ff_4_qn

  // Notes on the sheet:
  //   4 Bit Asynchronus Counter
endmodule

module Synchronus_Counter (
  input  in_1
);

  wire A_FF_q, A_FF_qn, and_1_out, and_2_out, B_FF_q, B_FF_qn, C_FF_q, C_FF_qn, clock_1_out, D_FF_q, D_FF_qn;

  Clock clock_1 (.out(clock_1_out));
  J_K_Flip_Flop D_FF (.J(in_1), .K(in_1), .clk(clock_1_out), .Q(D_FF_q), .Qn(D_FF_qn));  // open: preset, reset
  // NoConnect on D_FF_qn
  LED A (.in(A_FF_q));
  LED B (.in(B_FF_q));
  J_K_Flip_Flop C_FF (.J(D_FF_q), .K(D_FF_q), .clk(clock_1_out), .Q(C_FF_q), .Qn(C_FF_qn));  // open: preset, reset
  // NoConnect on C_FF_qn
  LED C (.in(C_FF_q));
  and and_1 (and_1_out, D_FF_q, C_FF_q);
  LED D (.in(D_FF_q));
  J_K_Flip_Flop B_FF (
    .J(and_1_out), .K(and_1_out), .clk(clock_1_out), .Q(B_FF_q), .Qn(B_FF_qn));  // open: preset, reset
  and and_2 (and_2_out, and_1_out, B_FF_q);
  // NoConnect on B_FF_qn
  J_K_Flip_Flop A_FF (
    .J(and_2_out), .K(and_2_out), .clk(clock_1_out), .Q(A_FF_q), .Qn(A_FF_qn));  // open: preset, reset
  // NoConnect on A_FF_qn

  // Notes on the sheet:
  //   4 Bit Synchronus Counter
endmodule

module MOD_10 (
  input  in_1
);

  wire A_FF_q, A_FF_qn, and_1_out, and_2_out, and_3_out, B_FF_q, B_FF_qn, C_FF_q, C_FF_qn, clock_1_out,
       D_FF_q, D_FF_qn;

  Clock clock_1 (.out(clock_1_out));
  J_K_Flip_Flop D_FF (
    .J(in_1), .K(in_1), .clk(clock_1_out), .Q(D_FF_q), .Qn(D_FF_qn), .reset(and_2_out));  // open: preset
  // NoConnect on D_FF_qn
  LED A (.in(A_FF_q));
  LED B (.in(B_FF_q));
  J_K_Flip_Flop C_FF (
    .J(D_FF_q), .K(D_FF_q), .clk(clock_1_out), .Q(C_FF_q), .Qn(C_FF_qn), .reset(and_2_out));  // open: preset
  // NoConnect on C_FF_qn
  LED C (.in(C_FF_q));
  and and_1 (and_1_out, D_FF_q, C_FF_q);
  LED D (.in(D_FF_q));
  J_K_Flip_Flop B_FF (
    .J(and_1_out), .K(and_1_out), .clk(clock_1_out), .Q(B_FF_q), .Qn(B_FF_qn), .reset(and_2_out));  // open: preset
  and and_2 (and_2_out, C_FF_q, A_FF_q);
  and and_3 (and_3_out, and_1_out, B_FF_q);
  // NoConnect on B_FF_qn
  J_K_Flip_Flop A_FF (
    .J(and_3_out), .K(and_3_out), .clk(clock_1_out), .Q(A_FF_q), .Qn(A_FF_qn), .reset(and_2_out));  // open: preset
  // NoConnect on A_FF_qn

  // Notes on the sheet:
  //   MOD-10 Synchronus Counter
endmodule

module Ripple_Down (
  input  in_1
);

  wire clock_1_out, j_k_ff_1_q, j_k_ff_1_qn, j_k_ff_2_q, j_k_ff_2_qn, j_k_ff_3_q, j_k_ff_3_qn, j_k_ff_4_qn;

  Clock clock_1 (.out(clock_1_out));
  J_K_Flip_Flop j_k_ff_1 (
    .J(in_1), .K(in_1), .clk(clock_1_out), .Q(j_k_ff_1_q), .Qn(j_k_ff_1_qn));  // open: preset, reset
  LED A (.in(j_k_ff_4_qn));
  J_K_Flip_Flop j_k_ff_2 (
    .J(in_1), .K(in_1), .clk(j_k_ff_1_q), .Q(j_k_ff_2_q), .Qn(j_k_ff_2_qn));  // open: preset, reset
  LED B (.in(j_k_ff_3_qn));
  LED C (.in(j_k_ff_2_qn));
  LED D (.in(j_k_ff_1_qn));
  J_K_Flip_Flop j_k_ff_3 (
    .J(in_1), .K(in_1), .clk(j_k_ff_2_q), .Q(j_k_ff_3_q), .Qn(j_k_ff_3_qn));  // open: preset, reset
  J_K_Flip_Flop j_k_ff_4 (.J(in_1), .K(in_1), .clk(j_k_ff_3_q), .Qn(j_k_ff_4_qn));  // open: Q, preset, reset

  // Notes on the sheet:
  //   4 Bit Asynchronus Up Counter
endmodule
