// Logisim project DLD_LAB_equation.circ as structural Verilog: 4 circuits, main circuit main
module main (
  input  in_1,
  input  in_2,
  input  in_3,
  output out_4
);

  Equation_2_from_app equation_2_from_app_1 (.A(in_1), .B(in_2), .C(in_3), .F(out_4));

  // Notes on the sheet:
  //   DLD Lab
  //   22 Dec 2023
  //   2103163
  //   F = ABC + ABC' + AB'C + A'BC
  //   = SOP(3,5,6,7)
  //   Exp Name: Implement Various Logic Function
endmodule

module Equation_1 (
  input  A,
  input  B,
  input  C,
  output F
);

  wire and_1_out, and_2_out, and_3_out, and_4_out;

  and and_1 (and_1_out, ~A, B, C);  // AND_Gate
  and and_2 (and_2_out, A, ~B, C);  // AND_Gate
  and and_3 (and_3_out, A, B, ~C);  // AND_Gate
  and and_4 (and_4_out, A, B, C);
  or or_1 (F, and_1_out, and_2_out, and_3_out, and_4_out);

  // Notes on the sheet:
  //   F = A'BC + AB'C + ABC' + ABC
  //   = SOP(3,5,6,7)
endmodule

module Equation_2_from_app (
  input  A,
  input  B,
  input  C,
  output F
);

  wire and_1_out, and_2_out, and_3_out;

  and and_1 (and_1_out, B, C);
  and and_2 (and_2_out, A, C);
  or or_1 (F, and_1_out, and_2_out, and_3_out);
  and and_3 (and_3_out, A, B);
endmodule

module From_expression (
  input  A,
  input  B,
  input  C,
  output F
);

  wire and_1_out, and_2_out, and_3_out, and_4_out, not_1_out, not_2_out, not_3_out;

  not not_1 (not_1_out, A);
  not not_2 (not_2_out, B);
  not not_3 (not_3_out, C);
  and and_1 (and_1_out, not_1_out, B, C);
  and and_2 (and_2_out, A, not_2_out, C);
  and and_3 (and_3_out, A, B, not_3_out);
  and and_4 (and_4_out, A, B, C);
  or or_1 (F, and_1_out, and_2_out, and_3_out, and_4_out);
endmodule
