// Logisim project abtojk.circ as structural Verilog: 2 circuits, main circuit main
module main (
  input  A,
  input  B,
  output out_3
);

  wire and_1_out, clock_1_out, j_k_ff_1_qn, not_1_out, xnor_1_out;

  not not_1 (not_1_out, A);
  Clock clock_1 (.out(clock_1_out));
  and and_1 (and_1_out, j_k_ff_1_qn, not_1_out);
  xnor xnor_1 (xnor_1_out, A, B);
  J_K_Flip_Flop j_k_ff_1 (
    .J(and_1_out), .K(xnor_1_out), .clk(clock_1_out), .Q(out_3), .Qn(j_k_ff_1_qn));  // open: preset, reset
endmodule

module jk (
  input  J,
  input  K,
  output QB,
  output Q
);

  wire and_1_out, and_2_out;

  and and_1 (and_1_out, QB, J);
  and and_2 (and_2_out, K, Q);
  nor nor_1 (QB, and_1_out, Q);
  nor nor_2 (Q, QB, and_2_out);
endmodule
