// Logisim project assignment.circ as structural Verilog: 3 circuits, main circuit main
module main (
  input  in_1,
  input  in_2,
  input  in_3,
  input  in_4,
  output out_5,
  output out_6
);

  wire and_1_out, and_2_out, not_1_out, not_2_out, not_3_out, or_1_out, xor_1_out;

  not not_1 (not_1_out, in_2);
  not not_2 (not_2_out, in_1);
  and and_1 (and_1_out, not_1_out, in_3);
  and and_2 (and_2_out, not_2_out, in_2);
  not not_3 (not_3_out, in_4);
  or or_1 (or_1_out, in_1, and_1_out);
  xor xor_1 (xor_1_out, and_2_out, in_4);
  or or_2 (out_6, and_2_out, not_3_out);
  or or_3 (out_5, or_1_out, xor_1_out);
endmodule

module auto (
  input  a,
  input  b,
  input  c,
  input  d,
  output x,
  output y
);

  wire and_1_out, and_2_out, and_3_out, not_1_out, not_2_out, not_3_out, xor_1_out;

  not not_1 (not_1_out, a);
  not not_2 (not_2_out, b);
  not not_3 (not_3_out, d);
  and and_1 (and_1_out, not_1_out, b);
  and and_2 (and_2_out, not_1_out, b);
  and and_3 (and_3_out, not_2_out, c);
  xor xor_1 (xor_1_out, and_1_out, d);
  or or_1 (y, and_2_out, not_3_out);
  or or_2 (x, a, and_3_out, xor_1_out);
endmodule

module flipflop (
  input  in_1,
  output [1:0] out_2
);

  wire clock_1_out, d_ff_1_qn;

  Clock clock_1 (.out(clock_1_out));
  J_K_Flip_Flop j_k_ff_1 (.J(in_1), .K(in_1), .clk(clock_1_out), .Q(out_2[0]));  // open: Qn, preset, reset
  LED led_1 (.in(out_2[0]));
  D_Flip_Flop d_ff_1 (.D(d_ff_1_qn), .clk(out_2[0]), .Q(out_2[1]), .Qn(d_ff_1_qn));  // open: preset, reset
  LED led_2 (.in(out_2[1]));

  // Notes on the sheet:
  //   Asynchronus 2 bit Counter
  //   Divided by 2 Counter
  //   Binary Counter
endmodule
