// Logisim project counter_design.circ as structural Verilog: 2 circuits, main circuit main
module main (
);

  wire A_qn, and_1_out, and_2_out, and_3_out, and_4_out, and_5_out, B_qn, C_qn, CLK_out, or_1_out, or_2_out,
       or_3_out, or_4_out;
  wire [3:0] D_q;

  Clock CLK (.out(CLK_out));
  and and_1 (and_1_out, B_qn, C_qn);
  or or_1 (or_1_out, and_1_out, A_qn);
  J_K_Flip_Flop D (.J(or_1_out), .K(1'b1), .clk(CLK_out), .Q(D_q[0]));  // open: Qn, preset, reset
  and and_2 (and_2_out, A_qn, D_q[0]);
  or or_2 (or_2_out, D_q[0], D_q[3]);
  Hex_Digit_Display hex_digit_display_1 (.value(D_q));  // open: dp
  J_K_Flip_Flop C (.J(and_2_out), .K(or_2_out), .clk(CLK_out), .Q(D_q[1]), .Qn(C_qn));  // open: preset, reset
  and and_3 (and_3_out, D_q[1], D_q[0]);
  and and_4 (and_4_out, D_q[0], D_q[1], A_qn);
  or or_3 (or_3_out, and_3_out, D_q[3]);
  J_K_Flip_Flop B (.J(and_4_out), .K(or_3_out), .clk(CLK_out), .Q(D_q[2]), .Qn(B_qn));  // open: preset, reset
  or or_4 (or_4_out, D_q[2], D_q[1], D_q[0]);
  and and_5 (and_5_out, D_q[0], D_q[1], D_q[2]);
  J_K_Flip_Flop A (.J(and_5_out), .K(or_4_out), .clk(CLK_out), .Q(D_q[3]), .Qn(A_qn));  // open: preset, reset

  // Notes on the sheet:
  //   Decade Counter Design
  //   Kaif Ahmed Khan
endmodule

module mod_10 (
);

  wire A_qn, and_1_out, and_2_out, and_3_out, clock_1_out;
  wire [3:0] D_q;

  Clock clock_1 (.out(clock_1_out));
  J_K_Flip_Flop D (.J(1'b1), .K(1'b1), .clk(clock_1_out), .Q(D_q[0]));  // open: Qn, preset, reset
  and and_1 (and_1_out, D_q[1], D_q[0]);
  and and_2 (and_2_out, A_qn, D_q[0]);
  J_K_Flip_Flop C (.J(and_2_out), .K(and_1_out), .clk(clock_1_out), .Q(D_q[1]));  // open: Qn, preset, reset
  Hex_Digit_Display hex_digit_display_1 (.value(D_q));  // open: dp
  J_K_Flip_Flop B (.J(and_1_out), .K(and_1_out), .clk(clock_1_out), .Q(D_q[2]));  // open: Qn, preset, reset
  and and_3 (and_3_out, D_q[0], D_q[1], D_q[2]);
  J_K_Flip_Flop A (.J(and_3_out), .K(D_q[0]), .clk(clock_1_out), .Q(D_q[3]), .Qn(A_qn));  // open: preset, reset
endmodule
