// Logisim project dld_lab_final.circ as structural Verilog: 2 circuits, main circuit main
module main (
  input  A,
  input  B,
  input  C,
  output Sum,
  output Carry
);

  wire and_1_out, and_2_out, xor_1_out;

  xor xor_1 (xor_1_out, A, B);
  and and_1 (and_1_out, A, B);
  and and_2 (and_2_out, xor_1_out, C);
  xor xor_2 (Sum, xor_1_out, C);
  or or_1 (Carry, and_2_out, and_1_out);

  // Notes on the sheet:
  //   Q1: Verification of Full Adder Circuit
endmodule

module MOD_16 (
  input  in_1,
  output [3:0] out_2
);

  wire and_1_out, and_2_out, CLK_out;

  Clock CLK (.out(CLK_out));
  J_K_Flip_Flop D_FF (.J(in_1), .K(in_1), .clk(CLK_out), .Q(out_2[0]));  // open: Qn, preset, reset
  J_K_Flip_Flop C_FF (.J(out_2[0]), .K(out_2[0]), .clk(CLK_out), .Q(out_2[1]));  // open: Qn, preset, reset
  LED A (.in(out_2[3]));
  LED B (.in(out_2[2]));
  LED C (.in(out_2[1]));
  and and_1 (and_1_out, out_2[0], out_2[1]);
  J_K_Flip_Flop B_FF (.J(and_1_out), .K(and_1_out), .clk(CLK_out), .Q(out_2[2]));  // open: Qn, preset, reset
  LED D (.in(out_2[0]));
  and and_2 (and_2_out, and_1_out, out_2[2]);
  J_K_Flip_Flop A_FF (.J(and_2_out), .K(and_2_out), .clk(CLK_out), .Q(out_2[3]));  // open: Qn, preset, reset

  // Notes on the sheet:
  //   Roll: 2103163
  //   MOD 16 Counter
endmodule
