// Logisim project practice_counter.circ as structural Verilog: 1 circuit, main circuit main
module main (
  input  in_1
);

  wire A_2_qn, B_2_qn, C_qn, clock_1_out;

  Clock clock_1 (.out(clock_1_out));
  LED A (.in(A_2_qn));
  LED B (.in(B_2_qn));
  J_K_Flip_Flop #(.trigger("falling")) C (
    .J(in_1), .clk(clock_1_out), .K(in_1), .Qn(C_qn));  // open: Q, preset, en, reset
  LED C_2 (.in(C_qn));
  J_K_Flip_Flop #(.trigger("falling")) B_2 (.J(in_1), .clk(C_qn), .K(in_1), .Qn(B_2_qn));  // open: Q, preset, en, reset
  J_K_Flip_Flop #(.trigger("falling")) A_2 (
    .J(in_1), .clk(B_2_qn), .K(in_1), .Qn(A_2_qn));  // open: Q, preset, en, reset

  // Notes on the sheet:
  //   3 Bit Ripple Counter
  //   - Falling Edge JK = Up Counter
  //   - Q' Output  = Up Counter
  //   Why Falling Edge makes it count up???
endmodule
