// Logisim project random_count.circ as structural Verilog: 3 circuits, main circuit main
module main (
);

  wire A_qn, and_1_out, and_2_out, and_3_out, and_4_out, and_5_out, B_qn, C_qn, clock_1_out, or_1_out,
       or_2_out, or_3_out;
  wire [2:0] C_q;

  and and_1 (and_1_out, C_q[1], C_q[2]);
  Clock clock_1 (.out(clock_1_out));
  or or_1 (or_1_out, and_1_out, and_2_out);
  and and_2 (and_2_out, B_qn, C_qn);
  T_Flip_Flop C (.T(or_1_out), .clk(clock_1_out), .Q(C_q[0]), .Qn(C_qn));  // open: reset, preset
  or or_2 (or_2_out, C_q[0], A_qn);
  Hex_Digit_Display hex_digit_display_1 (.value({1'b0, C_q}));  // open: dp
  J_K_Flip_Flop B (.J(or_2_out), .K(A_qn), .clk(clock_1_out), .Q(C_q[1]), .Qn(B_qn));  // open: preset, reset
  and and_3 (and_3_out, C_q[2], B_qn);
  and and_4 (and_4_out, C_q[2], C_qn);
  and and_5 (and_5_out, C_q[1], C_q[0], A_qn);
  or or_3 (or_3_out, and_3_out, and_4_out, and_5_out);
  D_Flip_Flop A (.D(or_3_out), .clk(clock_1_out), .Q(C_q[2]), .Qn(A_qn));  // open: preset, reset
endmodule

module random_2 (
);

  wire A_qn, and_1_out, and_2_out, and_3_out, B_qn, C_qn, clock_1_out, or_1_out, or_2_out, xnor_1_out;
  wire [2:0] C_q;

  Clock clock_1 (.out(clock_1_out));
  xnor xnor_1 (xnor_1_out, C_q[0], C_q[2]);
  T_Flip_Flop C (.T(xnor_1_out), .clk(clock_1_out), .Q(C_q[0]), .Qn(C_qn));  // open: reset, preset
  Hex_Digit_Display hex_digit_display_1 (.value({1'b0, C_q}));  // open: dp
  and and_1 (and_1_out, C_qn, A_qn);
  or or_1 (or_1_out, and_1_out, B_qn);
  D_Flip_Flop B (.D(or_1_out), .clk(clock_1_out), .Q(C_q[1]), .Qn(B_qn));  // open: preset, reset
  and and_2 (and_2_out, C_q[0], A_qn, B_qn);
  and and_3 (and_3_out, C_qn, C_q[1]);
  or or_2 (or_2_out, and_2_out, and_3_out);
  T_Flip_Flop A (.T(or_2_out), .clk(clock_1_out), .Q(C_q[2]), .Qn(A_qn));  // open: reset, preset
endmodule

module ls293 (
);

  _74193 u_74193_1 ();  // open: pin1, pin2, pin3, pin4, pin5, pin6, pin7, pin15, pin14, pin13, pin12, pin11, pin10, pin9
endmodule
