// Logisim project test.circ as structural Verilog: 1 circuit, main circuit main
module main (
  input  in_1
);

  wire clock_1_out, j_k_ff_1_q;

  Clock clock_1 (.out(clock_1_out));
  J_K_Flip_Flop j_k_ff_1 (.J(in_1), .K(in_1), .clk(clock_1_out), .Q(j_k_ff_1_q));  // open: Qn, preset, reset
  J_K_Flip_Flop j_k_ff_2 (.J(j_k_ff_1_q), .K(j_k_ff_1_q), .clk(clock_1_out));  // open: Q, Qn, preset, reset
endmodule
